# Fritzing sketch build-monitor (saved by Fritzing 0.9.3b)

parts:
  U1 = ESP32-30Pin [part_number=ESP32-30Pin]
  Part1 = 12 NeoPixel Ring [part_number=1643]

nets:
  VIN: U1.VIN, Part1.VDD
  GND: U1.GND, Part1.GND
  N1: U1.D13, Part1.IN

custom parts:
  ESP32-30Pin: Generic 30-Pin ESP32
  12 NeoPixel Ring: 12 ultra bright smart LED NeoPixels are arranged in a circle with 1.5" (37mm) outer diameter. The rings are 'chainable' - connect the output pin of one to the input pin of another. Use only one microcontroller pin to control as many as you can chain together! Each LED is addressable as the driver chip is inside the LED. Each one has ~18mA constant current drive so the color will be very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
