# Fritzing sketch motion-sensor (saved by Fritzing 0.9.3b)

parts:
  Part1 = HC-SR501 Body Sensor Module
  U1 = ESP32-30Pin [part_number=ESP32-30Pin]

nets:
  VCC: Part1.VCC, U1.VIN
  N1: Part1.OUT, U1.D13
  GND: Part1.GND, U1.GND

custom parts:
  HC-SR501 Body Sensor Module: Pyroelectric Infrared PIR Motion Sensor Detector Module
  ESP32-30Pin: Generic 30-Pin ESP32
