# Fritzing sketch remote-toggle (saved by Fritzing 0.9.4)

parts:
  WeMos_D1_Mini1 = WeMos D1 Mini
  S1 = Round Pushbutton
  LED1 = LED - 5mm [color="Red (633nm)" package="5 mm [THT]"]
  R1 = Resistor [tolerance=±5% resistance=1k package="0603 [SMD]"]
  R3 = Resistor [tolerance=±5% resistance=220 package=THT]

nets:
  N1: WeMos_D1_Mini1.5V, S1.leg1
  N2: WeMos_D1_Mini1.D1, S1.leg0, R1.Pin_1
  N3: WeMos_D1_Mini1.D2, LED1.anode
  N4: WeMos_D1_Mini1.G, R1.Pin_0, R3.Pin_0
  N5: LED1.cathode, R3.Pin_1
